# Fritzing sketch Riego_estado_sólido_uno (saved by Fritzing 0.9.4)
breadboards: 1

parts:
  U1 = RELAY-SOLIDSTATE [package=relay-s108t02]
  U2 = RELAY-SOLIDSTATE [package=relay-s108t02]
  U3 = RELAY-SOLIDSTATE [package=relay-s108t02]
  U4 = RELAY-SOLIDSTATE [package=relay-s108t02]
  Power_plug1 = Fuente
  Estabilizador_a_5V1 = LM2596 step down module
  L3 = Solenoid
  L4 = Solenoid
  R1 = 100 KΩ Resistor [package="1206 [SMD]"]
  R2 = 100 KΩ Resistor [package="1206 [SMD]"]
  R3 = 100 KΩ Resistor [package="1206 [SMD]"]
  R4 = 100 KΩ Resistor [package="1206 [SMD]"]
  MH-ET_LIVE_ESP32_DEVKIT1 = MH-ET LIVE ESP32 DEVKIT 38 pins

nets:
  N1: U1.T1, L3.pin2, R2.Pin_1
  N2: U1.T2, U2.T2, U3.T2, U4.T2, Power_plug1.VCC, Estabilizador_a_5V1.IN+
  N3: U1.-, U2.-, U3.-, U4.-, Power_plug1.GND, Estabilizador_a_5V1.IN-, Estabilizador_a_5V1.OUT-, R1.Pin_0, R2.Pin_0, R3.Pin_0, R4.Pin_0, MH-ET_LIVE_ESP32_DEVKIT1.GND#64
  N4: U2.T1, L3.pin1, R1.Pin_1
  N5: U3.T1, L4.pin2, R3.Pin_1
  N6: U4.T1, L4.pin1, R4.Pin_1
  N7: Estabilizador_a_5V1.OUT+, MH-ET_LIVE_ESP32_DEVKIT1.5V

notes:
  Entrada de 9V para las electrovalvulas
  5V
  Esquema Servidor_Riego

custom parts:
  Fuente: power plug
  LM2596 step down module: LM2596 DC-DC step down power supply module 3 A.
  100 KΩ Resistor: A generic resistor
  MH-ET LIVE ESP32 DEVKIT 38 pins: http://mh.nodebb.com/topic/2/mh-et-live-esp32-devkit
