# Fritzing sketch Servidor_AcuarioII (saved by Fritzing 0.9.4)

parts:
  Power_12V = Fuente
  Estabilizador_a_3_3V = LM2596 step down module
  LM7805 = Voltage Regulator - 5V [package="DPak [SMD]"]
  Relé_5V = KY-019 5V Relay Module [package="Breakout board"]
  Relé_5V_2 = KY-019 5V Relay Module [package="Breakout board"]
  Tira_Led_RGB = RGB LED (com. anode, rbg) [package="5 mm [THT]"]
  LEDS_5V = LEDs [package=led10mm]
  LM7809 = Voltage Regulator - 9V [package="DPak [SMD]"]
  U1 = ESP8266 WiFi Module [part_number=ESP8266]

nets:
  GND: Power_12V.GND, Estabilizador_a_3_3V.IN-, Estabilizador_a_3_3V.OUT-, LM7805.GND, Relé_5V.-, Relé_5V_2.-, Tira_Led_RGB.red_cathode, Tira_Led_RGB.blue_cathode, Tira_Led_RGB.green_cathode, LEDS_5V.C, LM7809.GND, U1.GND
  N1: Power_12V.VCC, Estabilizador_a_3_3V.IN+, Relé_5V.NO, LM7809.input_voltage
  N2: Estabilizador_a_3_3V.OUT+, U1.VCC
  N3: LM7805.input_voltage, LM7809.output_voltage
  N4: LM7805.output_voltage, Relé_5V.+, Relé_5V_2.+, Relé_5V_2.NO
  N5: Relé_5V.S, U1.GPIO_0
  N6: Relé_5V.Common, Tira_Led_RGB.common_anode
  N7: Relé_5V_2.S, U1.GPIO_2
  N8: Relé_5V_2.Common, LEDS_5V.A

notes:
  Esquema Servidor_Acuario
  12 V
  5 V

custom parts:
  Fuente: power plug
  LM2596 step down module: LM2596 DC-DC step down power supply module 3 A.
  KY-019 5V Relay Module: KY-019 5V Relay module, used to control AC circuits. (Special thanks to vanepp for fixing the PCB holes and other errors)
  Voltage Regulator - 9V: 9V DC Voltage Regulator
  ESP8266 WiFi Module: Generic WiFi Module based on the ESP8266 with onboard PCB antenna and UART communications
