# Fritzing sketch Servidor_Clima (saved by Fritzing 0.9.4)

parts:
  ESP32-WROOM-32 = MH-ET LIVE ESP32 DEVKIT 38 pins
  Módulo_tarjeta_SD = SD Card Module
  LCD_16x2 = LCD-16X2 [package=lcd-16x2]
  part = Trimmer Potentiometer [maximum_resistance=10kΩ package=THT]
  AM2302_(DHT22) = AM2302 Humidity and Temperature Sensor
  2N2222 = NPN-Transistor [package="TO92 [THT]"]
  R2 = 10 KΩ Resistor [package="0603 [SMD]"]
  1_K = 1 KΩ Resistor [package="0603 [SMD]"]
  1_K_2 = 1 KΩ Resistor [package="0603 [SMD]"]
  1_K_3 = 1 KΩ Resistor [package="0603 [SMD]"]

nets:
  3V3: ESP32-WROOM-32.3V3, Módulo_tarjeta_SD.+3.3, AM2302_(DHT22).VDD, 1_K_2.Pin_1
  N1: ESP32-WROOM-32.IO32, LCD_16x2.DB4
  N2: ESP32-WROOM-32.IO33, LCD_16x2.DB5
  N3: ESP32-WROOM-32.IO25, LCD_16x2.DB6
  N4: ESP32-WROOM-32.IO26, AM2302_(DHT22).DATA, 1_K_2.Pin_0
  N5: ESP32-WROOM-32.IO27, LCD_16x2.DB7
  N6: ESP32-WROOM-32.IO14, R2.Pin_0, 1_K.Pin_0
  N7: ESP32-WROOM-32.IO13, LCD_16x2.E
  5V: ESP32-WROOM-32.5V, LCD_16x2.VDD, part.leg1, 1_K_3.Pin_0
  GND: ESP32-WROOM-32.GND, Módulo_tarjeta_SD.GND, LCD_16x2.VSS, part.leg2, AM2302_(DHT22).GND, 2N2222.C
  N8: ESP32-WROOM-32.IO23, Módulo_tarjeta_SD.MOSI
  N9: ESP32-WROOM-32.IO19, Módulo_tarjeta_SD.MISO
  N10: ESP32-WROOM-32.IO18, Módulo_tarjeta_SD.SCK
  N11: ESP32-WROOM-32.IO5, Módulo_tarjeta_SD.CS
  N12: ESP32-WROOM-32.IO15, LCD_16x2.RS
  N13: LCD_16x2.VO, part.wiper
  N14: LCD_16x2.A, 1_K_3.Pin_1
  N15: LCD_16x2.K, 2N2222.E
  N16: 2N2222.B, R2.Pin_1, 1_K.Pin_1

notes:
  Esquema Servidor_Clima

custom parts:
  MH-ET LIVE ESP32 DEVKIT 38 pins: http://mh.nodebb.com/topic/2/mh-et-live-esp32-devkit
  SD Card Module: SD Card Module Slot Socket Reader For Arduino ARM MCU
  10 KΩ Resistor: A generic resistor (0.25W)
  1 KΩ Resistor: A generic resistor (0.25W)
