# Fritzing sketch Servidor_Riego (saved by Fritzing 0.9.4)

parts:
  Power_9V = Fuente
  Estabilizador_a_5V = LM2596 step down module
  Electrovalvula_1 = Solenoid
  Relé_2 = srd-05vdc-sl-c
  Relé_1 = srd-05vdc-sl-c
  2N2222 = NPN-Transistor [package="TO92 [THT]"]
  1_K = 1 KΩ Resistor [package="0603 [SMD]"]
  ESP32-WROOM-32 = MH-ET LIVE ESP32 DEVKIT 38 pins
  2N2222_2 = NPN-Transistor [package="TO92 [THT]"]
  1_K_2 = 1 KΩ Resistor [package="0603 [SMD]"]
  part = Rectifier Diode [part_number=1N4007 package="300 mil [THT]"]
  part_2 = Rectifier Diode [part_number=1N4007 package="300 mil [THT]"]
  Electrovalvula_2 = Solenoid
  Relé_3 = srd-05vdc-sl-c
  Relé_4 = srd-05vdc-sl-c
  1_K_3 = 1 KΩ Resistor [package="0603 [SMD]"]
  2N2222_3 = NPN-Transistor [package="TO92 [THT]"]
  2N2222_4 = NPN-Transistor [package="TO92 [THT]"]
  1_K_4 = 1 KΩ Resistor [package="0603 [SMD]"]
  part_3 = Rectifier Diode [part_number=1N4007 package="300 mil [THT]"]
  part_4 = Rectifier Diode [part_number=1N4007 package="300 mil [THT]"]

nets:
  GND: Power_9V.GND, Estabilizador_a_5V.IN-, Estabilizador_a_5V.OUT-, Relé_2.pin_3, Relé_1.pin_3, 2N2222.E, ESP32-WROOM-32.GND, 2N2222_2.E, Relé_3.pin_3, Relé_4.pin_3, 2N2222_3.E, 2N2222_4.E
  N1: Power_9V.VCC, Estabilizador_a_5V.IN+, Relé_2.pin_2, Relé_1.pin_2, Relé_3.pin_2, Relé_4.pin_2
  N2: Estabilizador_a_5V.OUT+, Relé_2.pin_1, Relé_1.pin_1, ESP32-WROOM-32.5V, part.cathode, part_2.cathode, Relé_3.pin_1, Relé_4.pin_1, part_3.cathode, part_4.cathode
  N3: Electrovalvula_1.pin1, Relé_1.pin_5
  N4: Electrovalvula_1.pin2, Relé_2.pin_5
  N5: Relé_2.pin_4, 2N2222.C, part.anode
  N6: Relé_1.pin_4, 2N2222_2.C, part_2.anode
  N7: 2N2222.B, 1_K.Pin_1
  N8: 1_K.Pin_0, ESP32-WROOM-32.IO26
  N9: ESP32-WROOM-32.IO33, 1_K_4.Pin_0
  N10: ESP32-WROOM-32.IO25, 1_K_3.Pin_0
  N11: ESP32-WROOM-32.IO27, 1_K_2.Pin_0
  N12: 2N2222_2.B, 1_K_2.Pin_1
  N13: Electrovalvula_2.pin1, Relé_3.pin_5
  N14: Electrovalvula_2.pin2, Relé_4.pin_5
  N15: Relé_3.pin_4, part_3.anode
  N16: Relé_4.pin_4, 2N2222_4.C, part_4.anode
  N17: 1_K_3.Pin_1, 2N2222_3.B
  N18: 2N2222_4.B, 1_K_4.Pin_1

notes:
  Esquema Servidor_Riego

custom parts:
  Fuente: power plug
  LM2596 step down module: LM2596 DC-DC step down power supply module 3 A.
  1 KΩ Resistor: A generic resistor (0.25W)
  MH-ET LIVE ESP32 DEVKIT 38 pins: http://mh.nodebb.com/topic/2/mh-et-live-esp32-devkit
  Rectifier Diode: A standard rectifier diode
